# Fritzing sketch Diagrama Esquematico (saved by Fritzing 0.9.3b)
breadboards: 2

parts:
  U1 = ESP32-38PinWide [part_number=ESP32-38PinWide]
  Componente1 = ACS712 Low Current Sensor Board v12
  Componente2 = ACS712 Low Current Sensor Board v12
  Part3 = Lilypad Battery Connect
  LED3 = LEDs [package=led10mm]
  LED4 = LEDs [package=led10mm]
  Part4 = Lilypad Battery Connect
  LED5 = RGB LED (com. cathode, rbg) [package="5 mm [THT]"]

nets:
  N1: U1.GPIO34, Componente2.VO
  N2: U1.GPIO26, LED5.green_anode
  N3: U1.GPIO27, LED5.blue_anode
  N4: U1.GPIO14, LED5.common_cathode
  GND: U1.GND, Componente1.GND, Componente2.GND
  5V: U1.VIN, Componente1.5V, Componente2.5V, LED5.red_anode
  N5: U1.GPIO19, Componente1.VO
  N6: Componente1.IP+, Part4.-
  N7: Componente1.IP-, LED3.A
  N8: Componente2.IP+, LED4.C
  N9: Componente2.IP-, Part3.-
  N10: Part3.+, LED4.A
  N11: LED3.C, Part4.+

custom parts:
  ESP32-38PinWide: Generic 38-Pin ESP32 with wide format (only access to one side of pins on a breadboard) based on Stephen Lilley's HiLetgo ESP-WROOM-32 ESP32 ESP-32S Development Board.
  LEDs: LEDs Standard schematic elements and footprints for 5mm, 3mm, 1206, and 0603 sized LEDs. 5mm - Spark Fun Electronics SKU : COM-00529 (and others)
